// Logisim project B_logisim.circ as structural Verilog: 7 circuits, main circuit main
module main (
);

  wire and_2_out, clk, clock_1_out, clock_2_out, counter_1_q, IgnoreCycle, Is16Bit, MemWrite, not_1_out,
       not_2_out, not_3_out, RegWrite, Result_Carry, Result_Carry_Alu, SHUTDOWNVal, SHUTDOWNWE, TempClr,
       TempWE, WDSelector, Zero;
  wire [1:0] ALUOp, MemWriteSrc, PCSelector, ResultCarrySrc, TempSelector;
  wire [2:0] ALUSrc, ResultSrc, rs1, rs2, rs3, rs4;
  wire [3:0] ALUControl, ALUResult, MemData, rd, Reg1, Reg2, Reg3, Reg4, Result, WriteData;
  wire [7:0] imm, MemAddress;
  wire [10:0] PC;
  wire [11:8] ImmConcatPC_3BBits;
  wire [11:11] ImmConcatPC_4BBits;
  wire [15:0] ConcatTempPC, multiplexer_1_out, NewPC, PCNext, PCPlus2, TempWrite;
  wire [15:12] Instr, TempOut;

  Clock clock_1 (.out(clock_1_out));
  Register #(.width(16)) register_1 (
    .D(PCNext), .clk(clk), .Q({ConcatTempPC[15:12], ImmConcatPC_3BBits[11], PC}));  // open: en, clr
  // Probe on PCNext
  not not_1 (not_1_out, SHUTDOWNVal);
  not not_2 (not_2_out, IgnoreCycle);
  Register #(.width(1)) SHUTDOWN (.D(1'b1), .en(SHUTDOWNWE), .clk(clk), .Q(SHUTDOWNVal));  // open: clr
  // Probe on imm
  // Probe on {Instr, ImmConcatPC_4BBits[11], ImmConcatPC_3BBits[10:8]}
  Multiplexer #(.enable("true"), .width(16)) multiplexer_1 (
    .in0(16'h1), .in1(16'h1), .out(multiplexer_1_out), .sel(Is16Bit));  // open: en
  and and_1 (clk, clock_1_out, not_1_out, not_2_out);
  // Probe on {ConcatTempPC[15:12], ImmConcatPC_3BBits[11], PC}
  // Probe on NewPC
  // Probe on NewPC
  Adder #(.width(16)) adder_1 (
    .a({ConcatTempPC[15:12], ImmConcatPC_3BBits[11], PC}), .b(multiplexer_1_out), .out(NewPC));  // open: cin, cout
  Multiplexer #(.enable("true"), .select(2), .width(16)) multiplexer_2 (
    .in0(NewPC), .in1(ConcatTempPC), .in2({ConcatTempPC[15:12], ImmConcatPC_3BBits, imm}),
    .in3({ConcatTempPC[15:12], ImmConcatPC_4BBits[11], ImmConcatPC_3BBits[10:8], imm}), .out(PCNext),
    .sel(PCSelector));  // open: en
  // Probe on PCSelector
  // Probe on ConcatTempPC
  // Probe on ConcatTempPC[15:12]
  // Probe on ConcatTempPC[11:0]
  // Probe on ImmConcatPC_3BBits[10:8]
  // Probe on {ConcatTempPC[15:12], ImmConcatPC_3BBits[11]}
  Clock clock_2 (.out(clock_2_out));
  Register #(.width(16)) TEMP (.D(TempWrite), .en(TempWE), .clk(clk), .Q({TempOut, ConcatTempPC[11:0]}));  // open: clr
  // Probe on PCNext
  // Probe on {ConcatTempPC[15:12], ImmConcatPC_3BBits, imm}
  // Probe on {ConcatTempPC[15:12], ImmConcatPC_4BBits[11], ImmConcatPC_3BBits[10:8], imm}
  Counter #(.max('h1), .trigger("falling"), .width(1)) counter_1 (
    .Q(counter_1_q), .clk(and_2_out), .clr(not_3_out));  // open: load, D, count, carry, up
  and and_2 (and_2_out, clock_2_out, Is16Bit);
  not not_3 (not_3_out, Is16Bit);
  instmem instmem_1 (
    .Reg1ForBBit(Reg1), .Zero(Zero), .Address({ConcatTempPC[15:12], ImmConcatPC_3BBits[11], PC}),
    .SHUTDOWN(SHUTDOWNWE), .TempWE(TempWE), .TempSelector(TempSelector), .PCSelector(PCSelector),
    .TempClr(TempClr), .is8or16(Is16Bit),
    .Instr({Instr, ImmConcatPC_4BBits[11], ImmConcatPC_3BBits[10:8], imm}));
  // Probe on {Instr, ImmConcatPC_4BBits[11], ImmConcatPC_3BBits[10:8], imm}
  // Probe on {ConcatTempPC[15:12], ImmConcatPC_4BBits[11], ImmConcatPC_3BBits[10:8], imm}
  and and_3 (IgnoreCycle, Is16Bit, counter_1_q);
  // Probe on {ImmConcatPC_4BBits[11], ImmConcatPC_3BBits[10:8]}
  // Probe on ConcatTempPC[15:12]
  Multiplexer #(.enable("true"), .select(2), .width(16)) multiplexer_3 (
    .in0({16{1'b0}}), .in1(PCPlus2), .out(TempWrite), .sel(TempSelector));  // open: in2, in3, en
  // Probe on TempSelector
  Adder #(.width(16)) adder_2 (
    .a({ConcatTempPC[15:12], ImmConcatPC_3BBits[11], PC}), .b(16'h2), .out(PCPlus2));  // open: cin, cout
  // Probe on TempWrite
  // Probe on {ImmConcatPC_4BBits[11], ImmConcatPC_3BBits[10:8]}
  // Probe on imm[3:0]
  // Probe on rs1
  // Probe on rs2
  maindecoder maindecoder_1 (
    .opcode({Instr, ImmConcatPC_4BBits[11], ImmConcatPC_3BBits[10:8]}), .is16Bit(Is16Bit), .rs1(rs1),
    .rs2(rs2), .rs3(rs3), .rs4(rs4), .rd(rd), .RegWrite(RegWrite), .ALUSrc(ALUSrc), .ALUOp(ALUOp),
    .ResultSrc(ResultSrc), .MemWrite(MemWrite), .MemWriteSrc(MemWriteSrc), .ResultCarrySrc(ResultCarrySrc),
    .WDSelector(WDSelector));
  aludecoder aludecoder_1 (.AluOp({Instr, ImmConcatPC_4BBits[11], ImmConcatPC_3BBits[10:8]}), .ALUControl(ALUControl));
  // Probe on ALUControl
  Multiplexer #(.select(3), .width(4)) multiplexer_4 (
    .in0(ALUResult), .in1(MemData), .in2(Reg4), .in3({ImmConcatPC_4BBits[11], ImmConcatPC_3BBits[10:8]}),
    .in4(imm[3:0]), .out(Result), .sel(ResultSrc));  // open: in5, in6, in7
  // Probe on ResultSrc
  // Probe on rs3
  // Probe on Result
  // Probe on rs4
  // Probe on rd
  Multiplexer #(.select(2)) multiplexer_5 (
    .in0(Result_Carry_Alu), .in1(1'b0), .in2(1'b1), .out(Result_Carry), .sel(ResultCarrySrc));  // open: in3
  // Probe on ResultCarrySrc
  // Probe on Reg1
  // Probe on Reg2
  regfile regfile_1 (
    .clk(clk), .A1(rs1), .A2(rs2), .A3(rs3), .A4(rs4), .A5(rd), .WD(Result), .CFWrite(Result_Carry),
    .WD2({ImmConcatPC_4BBits[11], ImmConcatPC_3BBits[10:8]}), .WD3(imm[3:0]), .WDSelector(WDSelector),
    .WE(RegWrite), .RD1(Reg1), .RD2(Reg2), .RD3(Reg3), .RD4(Reg4));
  // Probe on Result_Carry
  // Probe on Reg3
  // Probe on Reg4
  // Probe on {ImmConcatPC_4BBits[11], ImmConcatPC_3BBits[10:8]}
  // Probe on imm[3:0]
  alu alu_1 (
    .rs1(Reg1), .rs2(Reg2), .rs3(Reg3), .rs4(MemData), .rs5(Reg4), .ALUControl(ALUControl), .ALUSrc(ALUSrc),
    .imm(imm), .Zero(Zero), .ALUResult(ALUResult), .ALUResultCarry(Result_Carry_Alu), .MemAddress(MemAddress));
  // Probe on Result_Carry_Alu
  // Probe on Zero
  // Probe on ALUResult
  // Probe on MemAddress
  // Probe on WriteData
  Multiplexer #(.select(2), .width(4)) multiplexer_6 (
    .in0(ALUResult), .in1(Reg4), .out(WriteData), .sel(MemWriteSrc));  // open: in2, in3
  // Probe on MemWriteSrc
  // Probe on MemData
  datamem datamem_1 (.clk(clk), .WriteEnable(MemWrite), .WriteData(WriteData), .Address(MemAddress), .RD(MemData));

  // Other names for the same wires on the sheet: ImmConcatPC_4BBits (some bits) = {ConcatTempPC[15:12], ImmConcatPC_3BBits[10:8], imm};
  //   Instr[11:0] = {ImmConcatPC_4BBits[11], ImmConcatPC_3BBits[10:8], imm};
  //   InstrLastFour[3:0] = {ImmConcatPC_4BBits[11], ImmConcatPC_3BBits[10:8]};
  //   InstrLastThree[2:0] = ImmConcatPC_3BBits[10:8];
  //   opcode[7:0] = {Instr, ImmConcatPC_4BBits[11], ImmConcatPC_3BBits[10:8]};
  //   XImm[3:0] = {ImmConcatPC_4BBits[11], ImmConcatPC_3BBits[10:8]};
  //   PC[15:11] = {ConcatTempPC[15:12], ImmConcatPC_3BBits[11]};
  //   PCFirstFive[4:0] = {ConcatTempPC[15:12], ImmConcatPC_3BBits[11]};
  //   ImmConcatPC_3BBits (some bits) = {ConcatTempPC[15:12], imm}; PC_4bit[3:0] = ConcatTempPC[15:12];
  //   PCFirstFour[3:0] = ConcatTempPC[15:12]; YImm[3:0] = imm[3:0]; RegData[3:0] = Reg4;
  //   TempOut[11:0] = ConcatTempPC[11:0]; TempOut_12bit[11:0] = ConcatTempPC[11:0]

  // Notes on the sheet:
  //   Instruction Decoding
  //   PC
endmodule

module datamem (
  input  clk,
  input  WriteEnable,
  input  [3:0] WriteData,
  input  [7:0] Address,
  output [3:0] RD
);

  RAM #(.asyncread("true"), .dataWidth(4)) ram_1 (
    .addr(Address), .we(WriteEnable), .oe(1'b1), .clk(clk), .din(WriteData), .dout(RD));
endmodule

module regfile (
  input  clk,
  input  [2:0] A1,
  input  [2:0] A2,
  input  [2:0] A3,
  input  [2:0] A4,
  input  [3:0] A5,
  input  [3:0] WD,
  input  CFWrite,
  input  [3:0] WD2,
  input  [3:0] WD3,
  input  WDSelector,
  input  WE,
  output [3:0] RD1,
  output [3:0] RD2,
  output [3:0] RD3,
  output [3:0] RD4
);

  wire and_1_out, and_2_out, and_3_out, and_4_out, and_5_out, and_6_out, and_7_out, and_8_out, and_10_out,
       and_11_out, and_12_out, and_13_out, CF_q, w0, w1, w2, w3, w4, w5, w6, w7, wr0, wr0_1, wr1, wr2, wr2_3,
       wr3, wr4, wr5, wr5_6, wr6, wr7;
  wire [3:0] multiplexer_1_out, multiplexer_2_out, multiplexer_3_out, multiplexer_4_out, o0, o1, o2, o3, o4,
       o5, o6, o7;

  Decoder #(.select(4)) decoder_1 (
    .out0(wr0), .out1(wr1), .out2(wr2), .out3(wr3), .out4(wr4), .out5(wr5), .out6(wr6), .out7(wr5_6),
    .out8(wr0_1), .out9(wr2_3), .out10(wr7), .sel(A5));  // open: out11, out12, out13, out14, out15, en
  Register #(.width(4)) RA (.D(multiplexer_1_out), .en(w0), .clk(clk), .Q(o0));  // open: clr
  Multiplexer #(.width(4)) multiplexer_1 (.in0(WD), .in1(WD2), .out(multiplexer_1_out), .sel(WDSelector));
  Register #(.width(4)) RB (.D(multiplexer_2_out), .en(w1), .clk(clk), .Q(o1));  // open: clr
  Multiplexer #(.width(4)) multiplexer_2 (.in0(WD), .in1(WD3), .out(multiplexer_2_out), .sel(WDSelector));
  Register #(.width(4)) RC (.D(multiplexer_3_out), .en(w2), .clk(clk), .Q(o2));  // open: clr
  Multiplexer #(.width(4)) multiplexer_3 (.in0(WD), .in1(WD2), .out(multiplexer_3_out), .sel(WDSelector));
  Register #(.width(4)) RD (.D(multiplexer_4_out), .en(w3), .clk(clk), .Q(o3));  // open: clr
  Multiplexer #(.width(4)) multiplexer_4 (.in0(WD), .in1(WD3), .out(multiplexer_4_out), .sel(WDSelector));
  Register #(.width(4)) RE (.D(WD), .en(w4), .clk(clk), .Q(o4));  // open: clr
  and and_1 (and_1_out, wr0, WE);
  and and_2 (and_2_out, wr0_1, WE);
  and and_3 (and_3_out, wr1, WE);
  and and_4 (and_4_out, wr0_1, WE);
  and and_5 (and_5_out, wr2, WE);
  and and_6 (and_6_out, wr2_3, WE);
  and and_7 (and_7_out, wr3, WE);
  and and_8 (and_8_out, wr2_3, WE);
  and and_9 (w4, wr4, WE);
  and and_10 (and_10_out, wr5, WE);
  and and_11 (and_11_out, wr5_6, WE);
  and and_12 (and_12_out, wr6, WE);
  and and_13 (and_13_out, wr5_6, WE);
  and and_14 (w7, wr7, WE);
  Register #(.width(4)) ACC (.D(WD), .en(w5), .clk(clk), .Q(o5));  // open: clr
  Register #(.width(1)) CF (.D(CFWrite), .en(w6), .clk(clk), .Q(CF_q));  // open: clr
  or or_1 (w0, and_1_out, and_2_out);
  or or_2 (w1, and_3_out, and_4_out);
  or or_3 (w2, and_5_out, and_6_out);
  or or_4 (w3, and_7_out, and_8_out);
  or or_5 (w5, and_10_out, and_11_out);
  or or_6 (w6, and_12_out, and_13_out);
  // Probe on o6
  assign o6 = {{3{1'b0}}, CF_q};  // Bit_Extender bit_extender_1
  Register #(.width(4)) IOA (.D(WD), .en(w7), .clk(clk), .Q(o7));  // open: clr
  Multiplexer #(.select(3), .width(4)) multiplexer_5 (
    .in0(o0), .in1(o1), .in2(o2), .in3(o3), .in4(o4), .in5(o5), .in6(o6), .in7(o7), .out(RD1), .sel(A1));
  Multiplexer #(.select(3), .width(4)) multiplexer_6 (
    .in0(o0), .in1(o1), .in2(o2), .in3(o3), .in4(o4), .in5(o5), .in6(o6), .in7(o7), .out(RD2), .sel(A2));
  Multiplexer #(.select(3), .width(4)) multiplexer_7 (
    .in0(o0), .in1(o1), .in2(o2), .in3(o3), .in4(o4), .in5(o5), .in6(o6), .in7(o7), .out(RD3), .sel(A3));
  Multiplexer #(.select(3), .width(4)) multiplexer_8 (
    .in0(o0), .in1(o1), .in2(o2), .in3(o3), .in4(o4), .in5(o5), .in6(o6), .in7(o7), .out(RD4), .sel(A4));

  // Other names for the same wires on the sheet: WD1 = CFWrite
endmodule

module maindecoder (
  input  [7:0] opcode,
  input  is16Bit,
  output [2:0] rs1,
  output [2:0] rs2,
  output [2:0] rs3,
  output [2:0] rs4,
  output [3:0] rd,
  output RegWrite,
  output [2:0] ALUSrc,
  output [1:0] ALUOp,
  output [2:0] ResultSrc,
  output MemWrite,
  output [1:0] MemWriteSrc,
  output [1:0] ResultCarrySrc,
  output WDSelector
);

  wire AccAndRegTransfer, AccImm, AddcMba8, AddImm40, AddMba, and_1_out, and_2_out, and_3_out, and_4_out,
       and_5_out, and_6_out, and_7_out, and_8_out, and_9_out, and_10_out, and_14_out, and_15_out, and_16_out,
       and_17_out, and_18_out, and_19_out, and_34_out, and_41_out, and_42_out, and_43_out, and_44_out,
       and_45_out, and_57_out, and_58_out, and_59_out, and_60_out, and_61_out, and_62_out, and_63_out,
       and_65_out, and_66_out, and_67_out, and_68_out, AndBa18, AndImm42, AndMba21, BCD36, bitShifter,
       BranchZeroCheck, ClrCF, comparator_2_lt, comparator_3_gt, comparator_4_lt, comparator_5_lt,
       comparator_6_eq, comparator_7_eq, comparator_8_eq, comparator_9_eq, comparator_10_eq,
       comparator_11_eq, comparator_12_eq, comparator_13_eq, comparator_14_eq, comparator_15_eq,
       comparator_16_eq, comparator_17_eq, comparator_18_eq, comparator_19_eq, comparator_20_eq,
       comparator_21_eq, comparator_22_eq, comparator_23_eq, comparator_24_eq, comparator_25_eq,
       comparator_26_eq, comparator_27_eq, comparator_28_eq, comparator_29_eq, comparator_30_eq,
       comparator_31_eq, comparator_32_eq, comparator_33_eq, comparator_34_eq, comparator_35_eq,
       comparator_36_eq, comparator_37_eq, comparator_38_eq, comparator_39_eq, comparator_40_eq,
       comparator_41_eq, comparator_42_eq, comparator_43_eq, comparator_44_eq, comparator_45_eq,
       comparator_46_eq, comparator_47_eq, comparator_48_eq, comparator_49_eq, comparator_50_eq,
       comparator_51_eq, comparator_52_eq, comparator_53_eq, comparator_54_eq, comparator_55_eq,
       comparator_56_eq, comparator_57_eq, comparator_58_eq, comparator_59_eq, Dec3f, DecMba13, DecMdc15,
       DoubleOp_RegWrite, FromIoa32, FromMba4, FromMdc6, Inc31, IncMba12, IncMdc14, NoOp_MemWrite,
       NoOp_RegWrite, Nop, or_15_out, or_18_out, or_22_out, OrBa20, OrImm44, OrMba23, R4Imm, RA_RB, RC_RD,
       RD_ACC, RD_CF, RD_CF_ACC, RD_RA, RD_RB, RD_RC, RD_RD, RD_RE, RegIncrDecr, RegWrite_ImmediateOp,
       RS1_ACC, RS1_CF, RS1_RA, RS1_RB, RS1_RC, RS1_RD, RS1_RE, RS2_ACC, RS2_CF, RS2_RA, RS2_RB, RS2_RC,
       RS2_RD, RS2_RE, RS3_ACC, RS3_CF, RS3_RA, RS3_RB, RS3_RC, RS3_RD, RS3_RE, RS4_ACC, RS4_CF, RS4_IOA,
       RS4_RA, RS4_RB, RS4_RC, RS4_RD, RS4_RE, SetCF, SetReg4Imm, SingleOp_MemWrite,
       SingleOp_RegWrite_WithMem, SubcMba10, SubImm41, SubMba11, ToMba5, ToMdc7, ToReg, XorBa19, XorImm43,
       XorMba22;
  wire [4:0] Selector;

  // Probe on opcode[3:1]
  // Probe on opcode
  // Probe on 3'b101
  // Probe on opcode[3:1]
  Comparator #(.mode("unsigned")) comparator_1 (.a(opcode), .b(8'h4), .lt(bitShifter));  // open: gt, eq
  and and_1 (and_1_out, opcode[4], ~opcode[5], ~opcode[6], ~opcode[7]);  // AND_Gate
  Comparator #(.mode("unsigned"), .width(3)) comparator_2 (
    .a(opcode[3:1]), .b(3'b101), .lt(comparator_2_lt));  // open: gt, eq
  // Probe on 3'b101
  Comparator #(.mode("unsigned")) comparator_3 (.a(opcode), .b(8'h1f), .gt(comparator_3_gt));  // open: eq, lt
  Comparator #(.mode("unsigned")) comparator_4 (.a(opcode), .b(8'h2f), .lt(comparator_4_lt));  // open: gt, eq
  Comparator #(.mode("unsigned"), .width(3)) comparator_5 (
    .a(opcode[3:1]), .b(3'b101), .lt(comparator_5_lt));  // open: gt, eq
  // Probe on opcode[7:5]
  // Probe on opcode[7:4]
  Comparator #(.width(5)) comparator_6 (.a(opcode[7:3]), .b(5'b10100), .eq(comparator_6_eq));  // open: gt, lt
  Comparator #(.width(5)) comparator_7 (.a(opcode[7:3]), .b(5'b10101), .eq(comparator_7_eq));  // open: gt, lt
  Comparator #(.width(5)) comparator_8 (.a(opcode[7:3]), .b(5'b10110), .eq(comparator_8_eq));  // open: gt, lt
  Comparator #(.width(5)) comparator_9 (.a(opcode[7:3]), .b(5'b10111), .eq(comparator_9_eq));  // open: gt, lt
  Comparator #(.width(5)) comparator_10 (.a(opcode[7:3]), .b(5'b11000), .eq(comparator_10_eq));  // open: gt, lt
  Comparator #(.width(5)) comparator_11 (.a(opcode[7:3]), .b(5'b11001), .eq(comparator_11_eq));  // open: gt, lt
  Comparator #(.width(5)) comparator_12 (.a(opcode[7:3]), .b(5'b11011), .eq(comparator_12_eq));  // open: gt, lt
  Comparator #(.width(4)) comparator_13 (.a(opcode[7:4]), .b(4'b0101), .eq(comparator_13_eq));  // open: gt, lt
  Comparator #(.width(4)) comparator_14 (.a(opcode[7:4]), .b(4'b0110), .eq(comparator_14_eq));  // open: gt, lt
  Comparator comparator_15 (.a(opcode), .b(8'h46), .eq(comparator_15_eq));  // open: gt, lt
  or or_1 (NoOp_MemWrite, ToMba5, ToMdc7);
  or or_2 (DoubleOp_RegWrite, AddcMba8, SubcMba10, BCD36);
  or or_3 (SingleOp_RegWrite_WithMem, AddMba, SubMba11, AndBa18, XorBa19, OrBa20);
  and and_2 (and_2_out, and_1_out, comparator_2_lt);
  and and_3 (and_3_out, comparator_3_gt, comparator_4_lt, comparator_5_lt);
  or or_4 (RegWrite_ImmediateOp, AddImm40, SubImm41, AndImm42, XorImm43, OrImm44);
  and and_4 (and_4_out, is16Bit, comparator_6_eq);
  and and_5 (and_5_out, is16Bit, comparator_7_eq);
  and and_6 (and_6_out, is16Bit, comparator_8_eq);
  and and_7 (and_7_out, is16Bit, comparator_9_eq);
  and and_8 (and_8_out, is16Bit, comparator_10_eq);
  and and_9 (and_9_out, is16Bit, comparator_11_eq);
  and and_10 (and_10_out, is16Bit, comparator_12_eq);
  and and_11 (RA_RB, is16Bit, comparator_13_eq);
  and and_12 (RC_RD, is16Bit, comparator_14_eq);
  and and_13 (SetReg4Imm, comparator_15_eq, is16Bit);
  or or_5 (NoOp_RegWrite, FromMba4, FromMdc6);
  Comparator comparator_16 (.a(opcode), .b(8'h31), .eq(comparator_16_eq));  // open: gt, lt
  Comparator comparator_17 (.a(opcode), .b(8'h3f), .eq(comparator_17_eq));  // open: gt, lt
  or or_6 (SingleOp_MemWrite, IncMba12, DecMba13, IncMdc14, DecMdc15, AndMba21, XorMba22, OrMba23);
  or or_7 (AccAndRegTransfer, and_3_out, FromIoa32);
  or or_8 (RegIncrDecr, and_2_out, comparator_16_eq, comparator_17_eq);
  // Probe on opcode[7:3]
  not not_1 (ToReg, opcode[0]);
  // Probe on opcode[3:1]
  or or_9 (BranchZeroCheck, and_4_out, and_5_out, and_6_out, and_7_out, and_8_out, and_9_out, and_10_out);
  Comparator #(.mode("unsigned"), .width(3)) comparator_18 (
    .a(opcode[3:1]), .b(3'b000), .eq(comparator_18_eq));  // open: gt, lt
  Comparator #(.width(5)) comparator_19 (.a(opcode[7:3]), .b(5'b10100), .eq(comparator_19_eq));  // open: gt, lt
  Comparator #(.mode("unsigned"), .width(3)) comparator_20 (
    .a(opcode[3:1]), .b(3'b001), .eq(comparator_20_eq));  // open: gt, lt
  Comparator #(.width(5)) comparator_21 (.a(opcode[7:3]), .b(5'b10101), .eq(comparator_21_eq));  // open: gt, lt
  Comparator #(.mode("unsigned"), .width(3)) comparator_22 (
    .a(opcode[3:1]), .b(3'b010), .eq(comparator_22_eq));  // open: gt, lt
  Comparator #(.mode("unsigned"), .width(3)) comparator_23 (
    .a(opcode[3:1]), .b(3'b011), .eq(comparator_23_eq));  // open: gt, lt
  Comparator #(.width(5)) comparator_24 (.a(opcode[7:3]), .b(5'b11011), .eq(comparator_24_eq));  // open: gt, lt
  Comparator #(.mode("unsigned"), .width(3)) comparator_25 (
    .a(opcode[3:1]), .b(3'b100), .eq(comparator_25_eq));  // open: gt, lt
  Comparator #(.width(5)) comparator_26 (.a(opcode[7:3]), .b(5'b10110), .eq(comparator_26_eq));  // open: gt, lt
  Comparator #(.width(5)) comparator_27 (.a(opcode[7:3]), .b(5'b10111), .eq(comparator_27_eq));  // open: gt, lt
  and and_14 (and_14_out, RegIncrDecr, comparator_18_eq);
  and and_15 (and_15_out, RegIncrDecr, comparator_20_eq);
  and and_16 (and_16_out, RegIncrDecr, comparator_22_eq);
  and and_17 (and_17_out, RegIncrDecr, comparator_23_eq);
  and and_18 (and_18_out, RegIncrDecr, comparator_25_eq);
  Comparator comparator_28 (.a(opcode), .b({8{1'b0}}), .eq(comparator_28_eq));  // open: gt, lt
  Comparator comparator_29 (.a(opcode), .b(8'h1), .eq(comparator_29_eq));  // open: gt, lt
  Comparator #(.width(3)) comparator_30 (.a(opcode[7:5]), .b(3'b100), .eq(comparator_30_eq));  // open: gt, lt
  Comparator comparator_31 (.a(opcode), .b(8'h2), .eq(comparator_31_eq));  // open: gt, lt
  Comparator comparator_32 (.a(opcode), .b(8'h3), .eq(comparator_32_eq));  // open: gt, lt
  Comparator #(.width(5)) comparator_33 (.a(opcode[7:3]), .b(5'b11000), .eq(comparator_33_eq));  // open: gt, lt
  Comparator #(.width(5)) comparator_34 (.a(opcode[7:3]), .b(5'b11001), .eq(comparator_34_eq));  // open: gt, lt
  Priority_Encoder #(.select(5)) priority_encoder_1 (
    .in0(bitShifter), .in1(NoOp_RegWrite), .in2(NoOp_MemWrite), .in3(DoubleOp_RegWrite),
    .in4(SingleOp_RegWrite_WithMem), .in5(SingleOp_MemWrite), .in6(RegIncrDecr), .in7(AccAndRegTransfer),
    .in8(ClrCF), .in9(SetCF), .in10(Nop), .in11(RegWrite_ImmediateOp), .in12(BranchZeroCheck), .in13(AccImm),
    .in14(SetReg4Imm), .in15(RA_RB), .in16(RC_RD), .out(Selector));  // open: in17, in18, in19, in20, in21, in22, in23, in24, in25, in26, in27, in28, in29, in30, in31, gs, en_out, en_in
  Priority_Encoder priority_encoder_2 (
    .in0(RS1_RA), .in1(RS1_RB), .in2(RS1_RC), .in3(RS1_RD), .in4(RS1_RE), .in5(RS1_ACC), .in6(RS1_CF),
    .out(rs1));  // open: in7, en_in, gs, en_out
  or or_10 (RS1_RA, and_14_out, comparator_19_eq);
  or or_11 (RS1_RB, and_15_out, comparator_21_eq);
  buf or_12 (RS1_RC, and_16_out);  // OR_Gate
  or or_13 (RS1_RD, and_17_out, comparator_24_eq);
  buf or_14 (RS1_RE, and_18_out);  // OR_Gate
  and and_19 (and_19_out, is16Bit, comparator_30_eq);
  // Probe on Selector
  // Probe on rs1
  or or_15 (or_15_out, AndMba21, XorMba22, OrMba23, Inc31, FromIoa32, AddImm40, SubImm41, AndImm42, XorImm43, OrImm44, comparator_26_eq, comparator_27_eq, and_19_out, Dec3f);
  or or_16 (RS1_CF, comparator_31_eq, comparator_32_eq, BCD36, comparator_33_eq, comparator_34_eq);
  Multiplexer #(.select(5)) multiplexer_1 (
    .in0(1'b1), .in1(1'b1), .in2(1'b0), .in3(1'b1), .in4(1'b1), .in5(1'b0), .in6(1'b1), .in7(1'b1),
    .in8(1'b1), .in9(1'b1), .in10(1'b0), .in11(1'b1), .in12(1'b0), .in13(1'b1), .in14(1'b1), .in15(1'b1),
    .in16(1'b1), .out(RegWrite), .sel(Selector));  // open: in17, in18, in19, in20, in21, in22, in23, in24, in25, in26, in27, in28, in29, in30, in31
  or or_17 (RS1_ACC, comparator_28_eq, comparator_29_eq, AddcMba8, AddMba, SubcMba10, SubMba11, AndBa18, XorBa19, OrBa20, or_15_out);
  Multiplexer #(.select(5), .width(3)) multiplexer_2 (
    .in0(3'b000), .in1(3'b000), .in4(3'b001), .in5(3'b001), .in6(3'b010), .in9(3'b000), .in11(3'b011),
    .in12(3'b100), .out(ALUSrc), .sel(Selector));  // open: in2, in3, in7, in8, in10, in13, in14, in15, in16, in17, in18, in19, in20, in21, in22, in23, in24, in25, in26, in27, in28, in29, in30, in31
  Comparator comparator_35 (.a(opcode), .b(8'h2), .eq(comparator_35_eq));  // open: gt, lt
  Comparator comparator_36 (.a(opcode), .b(8'h3), .eq(comparator_36_eq));  // open: gt, lt
  // Probe on rs2
  Priority_Encoder priority_encoder_3 (
    .in0(RS2_RA), .in1(RS2_RB), .in2(RS2_RC), .in3(RS2_RD), .in4(RS2_RE), .in5(RS2_ACC), .in6(RS2_CF),
    .in7(RS2_CF), .out(rs2));  // open: en_in, gs, en_out
  or or_18 (or_18_out, AndMba21, XorMba22, OrMba23);
  or or_19 (RS2_RD, FromMdc6, ToMdc7, IncMdc14, DecMdc15);
  or or_20 (RS2_ACC, comparator_35_eq, comparator_36_eq, BCD36);
  Multiplexer #(.select(5)) multiplexer_3 (
    .in0(1'b0), .in1(1'b0), .in2(1'b1), .in3(1'b0), .in4(1'b0), .in5(1'b1), .in6(1'b0), .in7(1'b0),
    .in10(1'b0), .in11(1'b0), .out(MemWrite), .sel(Selector));  // open: in8, in9, in12, in13, in14, in15, in16, in17, in18, in19, in20, in21, in22, in23, in24, in25, in26, in27, in28, in29, in30, in31
  or or_21 (RS2_RB, FromMba4, ToMba5, AddcMba8, AddMba, SubcMba10, SubMba11, IncMba12, DecMba13, AndBa18, XorBa19, OrBa20, or_18_out);
  Multiplexer #(.select(5), .width(3)) multiplexer_4 (
    .in0(3'b000), .in1(3'b001), .in2(3'b001), .in3(3'b000), .in4(3'b000), .in5(3'b001), .in6(3'b000),
    .in7(3'b010), .in9(3'b000), .in11(3'b000), .in13(3'b011), .in14(3'b100), .out(ResultSrc), .sel(Selector));  // open: in8, in10, in12, in15, in16, in17, in18, in19, in20, in21, in22, in23, in24, in25, in26, in27, in28, in29, in30, in31
  Priority_Encoder priority_encoder_4 (
    .in0(RS3_RA), .in1(RS3_RB), .in2(RS3_RC), .in3(RS3_RD), .in4(RS3_RE), .in5(RS3_ACC), .in6(RS3_CF),
    .out(rs3));  // open: in7, en_in, gs, en_out
  // Probe on rs3
  or or_22 (or_22_out, AndMba21, XorMba22, OrMba23);
  or or_23 (RS3_RC, FromMdc6, ToMdc7, IncMdc14, DecMdc15);
  and and_20 (FromMdc6, opcode[0], opcode[1], opcode[2], ~opcode[3], ~opcode[4], ~opcode[5], ~opcode[6], ~opcode[7]);  // AND_Gate
  and and_21 (BCD36, ~opcode[0], opcode[1], opcode[2], ~opcode[3], opcode[4], opcode[5], ~opcode[6], ~opcode[7]);  // AND_Gate
  and and_22 (AndBa18, ~opcode[0], opcode[1], ~opcode[2], opcode[3], opcode[4], ~opcode[5], ~opcode[6], ~opcode[7]);  // AND_Gate
  and and_23 (ClrCF, ~opcode[0], opcode[1], ~opcode[2], opcode[3], ~opcode[4], opcode[5], ~opcode[6], ~opcode[7]);  // AND_Gate
  Multiplexer #(.select(5), .width(2)) multiplexer_5 (
    .in2(2'b01), .in5(2'b00), .in6(2'b00), .in9(2'b00), .out(MemWriteSrc), .sel(Selector));  // open: in0, in1, in3, in4, in7, in8, in10, in11, in12, in13, in14, in15, in16, in17, in18, in19, in20, in21, in22, in23, in24, in25, in26, in27, in28, in29, in30, in31
  or or_24 (RS3_RA, FromMba4, ToMba5, AddcMba8, AddMba, SubcMba10, SubMba11, IncMba12, DecMba13, AndBa18, XorBa19, OrBa20, or_22_out);
  and and_24 (ToMba5, opcode[0], ~opcode[1], opcode[2], ~opcode[3], ~opcode[4], ~opcode[5], ~opcode[6], ~opcode[7]);  // AND_Gate
  and and_25 (IncMba12, ~opcode[0], ~opcode[1], opcode[2], opcode[3], ~opcode[4], ~opcode[5], ~opcode[6], ~opcode[7]);  // AND_Gate
  and and_26 (IncMdc14, ~opcode[0], opcode[1], opcode[2], opcode[3], ~opcode[4], ~opcode[5], ~opcode[6], ~opcode[7]);  // AND_Gate
  and and_27 (AndMba21, opcode[0], ~opcode[1], opcode[2], opcode[3], opcode[4], ~opcode[5], ~opcode[6], ~opcode[7]);  // AND_Gate
  and and_28 (OrMba23, opcode[0], opcode[1], opcode[2], opcode[3], opcode[4], ~opcode[5], ~opcode[6], ~opcode[7]);  // AND_Gate
  and and_29 (Inc31, opcode[0], ~opcode[1], ~opcode[2], ~opcode[3], opcode[4], opcode[5], ~opcode[6], ~opcode[7]);  // AND_Gate
  and and_30 (AddImm40, ~opcode[0], ~opcode[1], ~opcode[2], ~opcode[3], ~opcode[4], ~opcode[5], opcode[6], ~opcode[7]);  // AND_Gate
  and and_31 (AndImm42, ~opcode[0], opcode[1], ~opcode[2], ~opcode[3], ~opcode[4], ~opcode[5], opcode[6], ~opcode[7]);  // AND_Gate
  and and_32 (OrImm44, ~opcode[0], ~opcode[1], opcode[2], ~opcode[3], ~opcode[4], ~opcode[5], opcode[6], ~opcode[7]);  // AND_Gate
  and and_33 (AccImm, opcode[4], opcode[5], opcode[6], ~opcode[7]);  // AND_Gate
  Multiplexer #(.select(5), .width(2)) multiplexer_6 (
    .in0(2'b00), .in3(2'b00), .in4(2'b00), .in8(2'b01), .in9(2'b10), .in10(2'b00), .out(ResultCarrySrc),
    .sel(Selector));  // open: in1, in2, in5, in6, in7, in11, in12, in13, in14, in15, in16, in17, in18, in19, in20, in21, in22, in23, in24, in25, in26, in27, in28, in29, in30, in31
  Comparator #(.mode("unsigned"), .width(3)) comparator_37 (
    .a(opcode[3:1]), .b(3'b000), .eq(comparator_37_eq));  // open: gt, lt
  Comparator #(.mode("unsigned"), .width(3)) comparator_38 (
    .a(opcode[3:1]), .b(3'b001), .eq(comparator_38_eq));  // open: gt, lt
  Comparator #(.mode("unsigned"), .width(3)) comparator_39 (
    .a(opcode[3:1]), .b(3'b010), .eq(comparator_39_eq));  // open: gt, lt
  Comparator #(.mode("unsigned"), .width(3)) comparator_40 (
    .a(opcode[3:1]), .b(3'b011), .eq(comparator_40_eq));  // open: gt, lt
  Comparator #(.mode("unsigned"), .width(3)) comparator_41 (
    .a(opcode[3:1]), .b(3'b100), .eq(comparator_41_eq));  // open: gt, lt
  Comparator comparator_42 (.a(opcode), .b(8'h5), .eq(comparator_42_eq));  // open: gt, lt
  Comparator comparator_43 (.a(opcode), .b(8'h7), .eq(comparator_43_eq));  // open: gt, lt
  and and_34 (and_34_out, AccAndRegTransfer, ToReg);
  and and_35 (FromIoa32, ~opcode[0], opcode[1], ~opcode[2], ~opcode[3], opcode[4], opcode[5], ~opcode[6], ~opcode[7]);  // AND_Gate
  and and_36 (ToMdc7, opcode[0], opcode[1], opcode[2], ~opcode[3], ~opcode[4], ~opcode[5], ~opcode[6], ~opcode[7]);  // AND_Gate
  and and_37 (AddcMba8, ~opcode[0], ~opcode[1], ~opcode[2], opcode[3], ~opcode[4], ~opcode[5], ~opcode[6], ~opcode[7]);  // AND_Gate
  and and_38 (SubMba11, opcode[0], opcode[1], ~opcode[2], opcode[3], ~opcode[4], ~opcode[5], ~opcode[6], ~opcode[7]);  // AND_Gate
  and and_39 (DecMba13, opcode[0], ~opcode[1], opcode[2], opcode[3], ~opcode[4], ~opcode[5], ~opcode[6], ~opcode[7]);  // AND_Gate
  and and_40 (DecMdc15, opcode[0], opcode[1], opcode[2], opcode[3], ~opcode[4], ~opcode[5], ~opcode[6], ~opcode[7]);  // AND_Gate
  // Probe on rs4
  Priority_Encoder priority_encoder_5 (
    .in0(RS4_RA), .in1(RS4_RB), .in2(RS4_RC), .in3(RS4_RD), .in4(RS4_RE), .in5(RS4_ACC), .in6(RS4_CF),
    .in7(RS4_IOA), .out(rs4));  // open: en_in, gs, en_out
  and and_41 (and_41_out, AccAndRegTransfer, comparator_37_eq);
  buf or_25 (RS4_RA, and_41_out);  // OR_Gate
  and and_42 (and_42_out, AccAndRegTransfer, comparator_38_eq);
  buf or_26 (RS4_RB, and_42_out);  // OR_Gate
  and and_43 (and_43_out, AccAndRegTransfer, comparator_39_eq);
  buf or_27 (RS4_RC, and_43_out);  // OR_Gate
  and and_44 (and_44_out, AccAndRegTransfer, comparator_40_eq);
  buf or_28 (RS4_RD, and_44_out);  // OR_Gate
  and and_45 (and_45_out, AccAndRegTransfer, comparator_41_eq);
  buf or_29 (RS4_RE, and_45_out);  // OR_Gate
  buf or_30 (RS4_IOA, FromIoa32);  // OR_Gate
  and and_46 (XorMba22, ~opcode[0], opcode[1], opcode[2], opcode[3], opcode[4], ~opcode[5], ~opcode[6], ~opcode[7]);  // AND_Gate
  and and_47 (SetCF, opcode[0], opcode[1], ~opcode[2], opcode[3], ~opcode[4], opcode[5], ~opcode[6], ~opcode[7]);  // AND_Gate
  and and_48 (Dec3f, opcode[0], opcode[1], opcode[2], opcode[3], opcode[4], opcode[5], ~opcode[6], ~opcode[7]);  // AND_Gate
  or or_31 (RS4_CF, AddcMba8, SubcMba10);
  or or_32 (RS4_ACC, comparator_42_eq, comparator_43_eq, and_34_out);
  and and_49 (SubImm41, opcode[0], ~opcode[1], ~opcode[2], ~opcode[3], ~opcode[4], ~opcode[5], opcode[6], ~opcode[7]);  // AND_Gate
  and and_50 (XorImm43, opcode[0], opcode[1], ~opcode[2], ~opcode[3], ~opcode[4], ~opcode[5], opcode[6], ~opcode[7]);  // AND_Gate
  and and_51 (R4Imm, ~opcode[0], opcode[1], opcode[2], ~opcode[3], ~opcode[4], ~opcode[5], opcode[6], ~opcode[7]);  // AND_Gate
  and and_52 (FromMba4, ~opcode[0], ~opcode[1], opcode[2], ~opcode[3], ~opcode[4], ~opcode[5], ~opcode[6], ~opcode[7]);  // AND_Gate
  and and_53 (SubcMba10, ~opcode[0], opcode[1], ~opcode[2], opcode[3], ~opcode[4], ~opcode[5], ~opcode[6], ~opcode[7]);  // AND_Gate
  and and_54 (AddMba, opcode[0], ~opcode[1], ~opcode[2], opcode[3], ~opcode[4], ~opcode[5], ~opcode[6], ~opcode[7]);  // AND_Gate
  Multiplexer #(.select(5)) multiplexer_7 (
    .in0(1'b0), .in1(1'b0), .in2(1'b0), .in3(1'b0), .in4(1'b0), .in5(1'b0), .in6(1'b0), .in7(1'b0),
    .in8(1'b0), .in9(1'b0), .in10(1'b0), .in11(1'b0), .in12(1'b0), .in13(1'b0), .in14(1'b0), .in15(1'b1),
    .in16(1'b1), .out(WDSelector), .sel(Selector));  // open: in17, in18, in19, in20, in21, in22, in23, in24, in25, in26, in27, in28, in29, in30, in31
  and and_55 (Nop, ~opcode[0], opcode[1], opcode[2], opcode[3], opcode[4], opcode[5], ~opcode[6], ~opcode[7]);  // AND_Gate
  Comparator #(.mode("unsigned"), .width(3)) comparator_44 (
    .a(opcode[3:1]), .b(3'b000), .eq(comparator_44_eq));  // open: gt, lt
  Comparator #(.mode("unsigned"), .width(3)) comparator_45 (
    .a(opcode[3:1]), .b(3'b000), .eq(comparator_45_eq));  // open: gt, lt
  Comparator #(.mode("unsigned"), .width(3)) comparator_46 (
    .a(opcode[3:1]), .b(3'b001), .eq(comparator_46_eq));  // open: gt, lt
  Comparator #(.mode("unsigned"), .width(3)) comparator_47 (
    .a(opcode[3:1]), .b(3'b001), .eq(comparator_47_eq));  // open: gt, lt
  Comparator #(.mode("unsigned"), .width(3)) comparator_48 (
    .a(opcode[3:1]), .b(3'b010), .eq(comparator_48_eq));  // open: gt, lt
  Comparator #(.mode("unsigned"), .width(3)) comparator_49 (
    .a(opcode[3:1]), .b(3'b010), .eq(comparator_49_eq));  // open: gt, lt
  and and_56 (XorBa19, opcode[0], opcode[1], ~opcode[2], opcode[3], opcode[4], ~opcode[5], ~opcode[6], ~opcode[7]);  // AND_Gate
  Priority_Encoder #(.select(4)) priority_encoder_6 (
    .in0(RD_RA), .in1(RD_RB), .in2(RD_RC), .in3(RD_RD), .in4(RD_RE), .in5(RD_ACC), .in6(RD_CF),
    .in7(RD_CF_ACC), .in8(RA_RB), .in9(RC_RD), .out(rd));  // open: in10, in11, in12, in13, in14, in15, gs, en_out, en_in
  and and_57 (and_57_out, AccAndRegTransfer, ToReg, comparator_44_eq);
  and and_58 (and_58_out, RegIncrDecr, comparator_45_eq);
  and and_59 (and_59_out, AccAndRegTransfer, ToReg, comparator_46_eq);
  and and_60 (and_60_out, RegIncrDecr, comparator_47_eq);
  and and_61 (and_61_out, AccAndRegTransfer, ToReg, comparator_48_eq);
  and and_62 (and_62_out, RegIncrDecr, comparator_49_eq);
  Comparator comparator_50 (.a(opcode), .b(8'h1), .eq(comparator_50_eq));  // open: gt, lt
  Comparator comparator_51 (.a(opcode), .b({8{1'b0}}), .eq(comparator_51_eq));  // open: gt, lt
  Comparator comparator_52 (.a(opcode), .b(8'h1a), .eq(comparator_52_eq));  // open: gt, lt
  Comparator comparator_53 (.a(opcode), .b(8'h1c), .eq(comparator_53_eq));  // open: gt, lt
  and and_63 (and_63_out, AccAndRegTransfer, opcode[0]);
  Comparator comparator_54 (.a(opcode), .b(8'h2), .eq(comparator_54_eq));  // open: gt, lt
  Comparator comparator_55 (.a(opcode), .b(8'h3), .eq(comparator_55_eq));  // open: gt, lt
  // Probe on rd
  or or_33 (RD_RA, and_57_out, and_58_out);
  or or_34 (RD_RB, and_59_out, and_60_out);
  or or_35 (RD_RC, and_61_out, and_62_out);
  or or_36 (RD_ACC, FromMba4, comparator_50_eq, comparator_51_eq, FromMdc6, comparator_52_eq, comparator_53_eq, AndBa18, XorBa19, OrBa20, and_63_out, FromIoa32, Inc31, Dec3f, AddImm40, SubImm41, AndImm42, XorImm43, OrImm44, AccImm);
  or or_37 (RD_CF_ACC, comparator_54_eq, comparator_55_eq, AddcMba8, AddMba, SubcMba10, SubMba11, BCD36);
  or or_38 (RD_CF, ClrCF, SetCF);
  and and_64 (OrBa20, ~opcode[0], ~opcode[1], opcode[2], opcode[3], opcode[4], ~opcode[5], ~opcode[6], ~opcode[7]);  // AND_Gate
  Comparator #(.mode("unsigned"), .width(3)) comparator_56 (
    .a(opcode[3:1]), .b(3'b011), .eq(comparator_56_eq));  // open: gt, lt
  Comparator #(.mode("unsigned"), .width(3)) comparator_57 (
    .a(opcode[3:1]), .b(3'b011), .eq(comparator_57_eq));  // open: gt, lt
  Comparator #(.mode("unsigned"), .width(3)) comparator_58 (
    .a(opcode[3:1]), .b(3'b100), .eq(comparator_58_eq));  // open: gt, lt
  Comparator #(.mode("unsigned"), .width(3)) comparator_59 (
    .a(opcode[3:1]), .b(3'b100), .eq(comparator_59_eq));  // open: gt, lt
  and and_65 (and_65_out, AccAndRegTransfer, ToReg, comparator_56_eq);
  and and_66 (and_66_out, RegIncrDecr, comparator_57_eq);
  and and_67 (and_67_out, AccAndRegTransfer, ToReg, comparator_58_eq);
  and and_68 (and_68_out, RegIncrDecr, comparator_59_eq);
  or or_39 (RD_RD, and_65_out, and_66_out);
  or or_40 (RD_RE, and_67_out, R4Imm, and_68_out);

  // Other names for the same wires on the sheet: FromReg = opcode[0]; RegBit[2:0] = opcode[3:1];
  //   FiveFirstIn16Bits[4:0] = opcode[7:3]; FourFirstIn16Bits[3:0] = opcode[7:4];
  //   ThreeFirstIn16Bits[2:0] = opcode[7:5]; RD_RA_RB = RA_RB; RD_RC_RD = RC_RD; RegResultSrc[2:0] = ResultSrc;
  //   RS2_IOA = RS2_CF; SetACCImm = AccImm

  // Notes on the sheet:
  //   Instruction 33
  //   WriteData
endmodule

module instmem (
  input  [3:0] Reg1ForBBit,
  input  Zero,
  input  [15:0] Address,
  output SHUTDOWN,
  output TempWE,
  output [1:0] TempSelector,
  output [1:0] PCSelector,
  output TempClr,
  output is8or16,
  output [15:0] Instr
);

  wire and_2_out, and_3_out, and_4_out, and_5_out, and_6_out, and_7_out, and_8_out, and_9_out, and_10_out,
       and_11_out, call, comparator_2_eq, comparator_5_eq, comparator_6_eq, comparator_7_eq, comparator_8_eq,
       comparator_9_eq, comparator_10_eq, comparator_11_eq, comparator_12_eq, comparator_13_eq,
       comparator_14_eq, comparator_15_eq, ImmConcatPC, ImmConcatPC1, ImmConcatPC2, is8or16_t,
       multiplexer_2_out, not_1_out, not_2_out, not_3_out, not_4_out, not_5_out, not_7_out, NotRet;
  wire [15:0] i, shifter_1_out;

  ROM #(.addrWidth(16), .dataWidth(16)) rom_1 (.addr(Address), .data(i));
  Comparator #(.mode("unsigned"), .width(16)) comparator_1 (.a(i), .b(16'h100), .lt(is8or16_t));  // open: gt, eq
  Shifter #(.width(16)) shifter_1 (.in(i), .\dist (4'b1000), .out(shifter_1_out));
  Comparator #(.width(4)) comparator_2 (.a(Instr[15:12]), .b(4'b1111), .eq(comparator_2_eq));  // open: gt, lt
  // Probe on Instr
  Multiplexer #(.width(16)) multiplexer_1 (.in0(i), .in1(shifter_1_out), .out(Instr), .sel(is8or16_t));
  and and_1 (call, is8or16, comparator_2_eq);
  // Probe on i
  Multiplexer #(.select(2)) multiplexer_2 (
    .in0(Reg1ForBBit[0]), .in1(Reg1ForBBit[1]), .in2(Reg1ForBBit[2]), .in3(Reg1ForBBit[3]),
    .out(multiplexer_2_out), .sel(Instr[12:11]));
  Comparator #(.width(16)) comparator_3 (.a(i), .b(16'h373e), .eq(SHUTDOWN));  // open: gt, lt
  Comparator #(.width(16)) comparator_4 (.a(i), .b(16'h2e), .eq(TempClr));  // open: gt, lt
  // Probe on Instr[15:13]
  // Probe on Instr[15:12]
  // Probe on Instr[15:11]
  // Probe on Instr[12:11]
  not not_1 (not_1_out, Zero);
  Comparator #(.width(5)) comparator_5 (.a(Instr[15:11]), .b(5'b10100), .eq(comparator_5_eq));  // open: gt, lt
  not not_2 (not_2_out, Zero);
  Comparator #(.width(5)) comparator_6 (.a(Instr[15:11]), .b(5'b10101), .eq(comparator_6_eq));  // open: gt, lt
  not not_3 (not_3_out, Zero);
  Comparator #(.width(5)) comparator_7 (.a(Instr[15:11]), .b(5'b10110), .eq(comparator_7_eq));  // open: gt, lt
  Comparator #(.width(5)) comparator_8 (.a(Instr[15:11]), .b(5'b10111), .eq(comparator_8_eq));  // open: gt, lt
  Comparator #(.width(5)) comparator_9 (.a(Instr[15:11]), .b(5'b11000), .eq(comparator_9_eq));  // open: gt, lt
  not not_4 (not_4_out, Zero);
  Comparator #(.width(5)) comparator_10 (.a(Instr[15:11]), .b(5'b11001), .eq(comparator_10_eq));  // open: gt, lt
  not not_5 (not_5_out, Zero);
  Comparator #(.width(5)) comparator_11 (.a(Instr[15:11]), .b(5'b11011), .eq(comparator_11_eq));  // open: gt, lt
  Comparator #(.width(3)) comparator_12 (.a(Instr[15:13]), .b(3'b100), .eq(comparator_12_eq));  // open: gt, lt
  Comparator #(.width(1)) comparator_13 (.a(multiplexer_2_out), .b(1'b1), .eq(comparator_13_eq));  // open: gt, lt
  Comparator #(.width(4)) comparator_14 (.a(Instr[15:12]), .b(4'b1110), .eq(comparator_14_eq));  // open: gt, lt
  Comparator #(.width(4)) comparator_15 (.a(Instr[15:12]), .b(4'b1111), .eq(comparator_15_eq));  // open: gt, lt
  or or_1 (TempWE, TempClr, call);
  Priority_Encoder #(.select(2)) priority_encoder_1 (
    .in0(TempClr), .in1(call), .out(TempSelector));  // open: in2, in3, gs, en_out, en_in
  Priority_Encoder #(.select(2)) priority_encoder_2 (
    .in0(NotRet), .in1(TempClr), .in2(ImmConcatPC1), .in3(ImmConcatPC2), .out(PCSelector));  // open: gs, en_out, en_in
  not not_6 (is8or16, is8or16_t);
  and and_2 (and_2_out, not_1_out, comparator_5_eq);
  and and_3 (and_3_out, not_2_out, comparator_6_eq);
  and and_4 (and_4_out, not_3_out, comparator_7_eq);
  and and_5 (and_5_out, Zero, comparator_8_eq);
  and and_6 (and_6_out, Zero, comparator_9_eq);
  and and_7 (and_7_out, not_4_out, comparator_10_eq);
  and and_8 (and_8_out, not_5_out, comparator_11_eq);
  and and_9 (and_9_out, comparator_12_eq, comparator_13_eq);
  and and_10 (and_10_out, is8or16, comparator_14_eq);
  and and_11 (and_11_out, is8or16, comparator_15_eq);
  not not_7 (not_7_out, TempClr);
  and and_12 (NotRet, ~ImmConcatPC, not_7_out);  // AND_Gate
  or or_2 (ImmConcatPC1, and_2_out, and_3_out, and_4_out, and_5_out, and_6_out, and_7_out, and_8_out, and_9_out);
  or or_3 (ImmConcatPC2, and_10_out, and_11_out);
  or or_4 (ImmConcatPC, ImmConcatPC1, ImmConcatPC2);

  // Other names for the same wires on the sheet: FiveFirstIn16Bits[4:0] = Instr[15:11]; KBits[1:0] = Instr[12:11];
  //   FourFirstIn16Bits[3:0] = Instr[15:12]; ThreeFirstIn16Bits[2:0] = Instr[15:13]; Is16bit = is8or16; ret = TempClr;
  //   shiftLeft8 = is8or16_t

  // Notes on the sheet:
  //   contents of rom_1 (hex, n*v repeats v):
  //   3e 20 22 24 26 28 21 23 25 27 29
endmodule

module alu (
  input  [3:0] rs1,
  input  [3:0] rs2,
  input  [3:0] rs3,
  input  [3:0] rs4,
  input  [3:0] rs5,
  input  [3:0] ALUControl,
  input  [2:0] ALUSrc,
  input  [7:0] imm,
  output Zero,
  output [3:0] ALUResult,
  output ALUResultCarry,
  output [7:0] MemAddress
);

  wire ALURCLeft, ALURCRight, comparator_1_gt, comparator_2_eq, comparator_3_eq, comparator_4_eq,
       comparator_5_eq, comparator_6_eq, comparator_7_eq, comparator_8_eq, comparator_9_eq, MemAddCarry,
       MemSubAddUnderflow, MemSubUnderflow, or_2_out, or_3_out, Triple_Add_Carry;
  wire [2:0] selector;
  wire [3:0] adder_3_out, adder_5_out, and_1_out, CF_ACC_LEFT, CF_ACC_RIGHT, MemAdd, MemDecr, MemIncr,
       MemSub, MemSubAdd, multiplexer_1_out, multiplexer_2_out, or_1_out, shifter_1_out, shifter_2_out,
       subtractor_1_out, Triple_Add, xor_1_out;
  wire [7:5] shifter_3_out, shifter_4_out;

  // Probe on {rs2, rs3}
  Multiplexer #(.select(3), .width(4)) multiplexer_1 (
    .in0(rs2), .in1(rs4), .in2(4'b0001), .in3(imm[3:0]), .in4(4'b0000), .out(multiplexer_1_out), .sel(ALUSrc));  // open: in5, in6, in7
  // Probe on ALUSrc
  // Probe on {rs1, rs2}
  Adder #(.width(4)) adder_1 (.a(rs1), .b(rs4), .out(MemAdd), .cout(MemAddCarry));  // open: cin
  Adder #(.width(4)) adder_2 (.a(rs1), .b(rs4), .out(MemSub), .cout(MemSubUnderflow));  // open: cin
  Adder #(.width(4)) adder_3 (.a(rs2), .b(4'b0110), .out(adder_3_out));  // open: cin, cout
  Comparator #(.mode("unsigned"), .width(4)) comparator_1 (.a(rs2), .b(4'b1001), .gt(comparator_1_gt));  // open: eq, lt
  Comparator #(.mode("unsigned"), .width(4)) comparator_2 (.a(rs1), .b(4'b0001), .eq(comparator_2_eq));  // open: gt, lt
  // Probe on MemAddCarry
  // Probe on MemAdd
  // Probe on MemSubUnderflow
  // Probe on MemSub
  Adder #(.width(4)) adder_4 (.a(MemSub), .b(rs5), .out(MemSubAdd), .cin(MemSubUnderflow), .cout(MemSubAddUnderflow));
  Adder #(.width(4)) adder_5 (.a(rs1), .b(multiplexer_1_out), .out(adder_5_out));  // open: cin, cout
  Subtractor #(.width(4)) subtractor_1 (.a(rs1), .b(multiplexer_1_out), .out(subtractor_1_out));  // open: bin, bout
  assign and_1_out = rs1 & multiplexer_1_out;  // AND_Gate and_1, 4 bits wide
  assign or_1_out = rs1 | multiplexer_1_out;  // OR_Gate or_1, 4 bits wide
  Shifter #(.shift("lr"), .width(4)) shifter_1 (.in(rs1), .\dist (2'b01), .out(shifter_1_out));
  Shifter #(.width(4)) shifter_2 (.in(rs1), .\dist (2'b01), .out(shifter_2_out));
  // Probe on adder_3_out
  or or_2 (or_2_out, comparator_1_gt, comparator_2_eq);
  // Probe on Triple_Add
  Adder #(.width(4)) adder_6 (.a(MemAdd), .b(rs5), .out(Triple_Add), .cin(MemAddCarry), .cout(Triple_Add_Carry));
  // Probe on Triple_Add_Carry
  // Probe on MemSubAdd
  // Probe on MemSubAddUnderflow
  assign xor_1_out = rs1 ^ multiplexer_1_out;  // XOR_Gate xor_1, 4 bits wide
  Multiplexer #(.width(4)) multiplexer_2 (.in1(adder_3_out), .out(multiplexer_2_out), .sel(or_2_out));  // open: in0
  // Probe on {shifter_3_out, ALURCLeft, CF_ACC_LEFT}
  Shifter shifter_3 (.in({rs1, rs2}), .\dist (3'b001), .out({shifter_3_out, ALURCLeft, CF_ACC_LEFT}));
  // Probe on {shifter_4_out, ALURCRight, CF_ACC_RIGHT}
  Shifter #(.shift("lr")) shifter_4 (.in({rs1, rs2}), .\dist (3'b001), .out({shifter_4_out, ALURCRight, CF_ACC_RIGHT}));
  Multiplexer #(.select(4), .width(4)) multiplexer_3 (
    .in0(adder_5_out), .in1(subtractor_1_out), .in2(and_1_out), .in3(or_1_out), .in4(shifter_1_out),
    .in5(shifter_2_out), .in6(CF_ACC_RIGHT), .in7(CF_ACC_LEFT), .in8(Triple_Add), .in9(MemAdd),
    .in10(MemSubAdd), .in11(MemSub), .in12(MemIncr), .in13(MemDecr), .in14(xor_1_out),
    .in15(multiplexer_2_out), .out(ALUResult), .sel(ALUControl));
  // Probe on ALUResult
  // Probe on ALUControl
  // Probe on CF_ACC_LEFT
  // Probe on ALURCLeft
  or or_3 (or_3_out, ALUResult[0], ALUResult[1], ALUResult[2], ALUResult[3]);
  Comparator #(.width(4)) comparator_3 (.a(ALUControl), .b(4'b0110), .eq(comparator_3_eq));  // open: gt, lt
  Comparator #(.width(4)) comparator_4 (.a(ALUControl), .b(4'b0111), .eq(comparator_4_eq));  // open: gt, lt
  Comparator #(.width(4)) comparator_5 (.a(ALUControl), .b(4'b1000), .eq(comparator_5_eq));  // open: gt, lt
  Comparator #(.width(4)) comparator_6 (.a(ALUControl), .b(4'b1001), .eq(comparator_6_eq));  // open: gt, lt
  Comparator #(.width(4)) comparator_7 (.a(ALUControl), .b(4'b1010), .eq(comparator_7_eq));  // open: gt, lt
  Comparator #(.width(4)) comparator_8 (.a(ALUControl), .b(4'b1011), .eq(comparator_8_eq));  // open: gt, lt
  Comparator #(.width(4)) comparator_9 (.a(ALUControl), .b(4'b1111), .eq(comparator_9_eq));  // open: gt, lt
  Adder #(.width(4)) adder_7 (.a(rs4), .b(4'b0001), .out(MemIncr));  // open: cin, cout
  Subtractor #(.width(4)) subtractor_2 (.a(rs4), .b(4'b0001), .out(MemDecr));  // open: bin, bout
  not not_1 (Zero, or_3_out);
  Multiplexer #(.select(3)) multiplexer_4 (
    .in0(ALURCRight), .in1(ALURCLeft), .in2(Triple_Add_Carry), .in3(MemAddCarry), .in4(MemSubAddUnderflow),
    .in5(MemSubUnderflow), .in6(1'b1), .out(ALUResultCarry), .sel(selector));  // open: in7
  // Probe on MemIncr
  // Probe on MemDecr
  Priority_Encoder priority_encoder_1 (
    .in0(comparator_3_eq), .in1(comparator_4_eq), .in2(comparator_5_eq), .in3(comparator_6_eq),
    .in4(comparator_7_eq), .in5(comparator_8_eq), .in6(comparator_9_eq), .out(selector));  // open: in7, en_in, gs, en_out

  assign MemAddress = {rs2, rs3};

  // Other names for the same wires on the sheet: CF_CONCAT[7:0] = {rs1, rs2}; SrcA[3:0] = rs1; imm_t[3:0] = imm[3:0];
  //   immlong[7:0] = imm; MEM_CONCAT[7:0] = {rs2, rs3}; SrcC[3:0] = rs3; SrcB[3:0] = rs2; SrcD[3:0] = rs4;
  //   SrcE[3:0] = rs5
endmodule

module aludecoder (
  input  [7:0] AluOp,
  output [3:0] ALUControl
);

  wire AddcMba8, AddImm40, AddMba, and_2_out, and_3_out, AndBa18, AndImm42, AndMba21, BCD36, comparator_1_eq,
       comparator_2_eq, comparator_5_lt, comparator_6_gt, comparator_7_lt, comparator_8_eq, comparator_9_eq,
       comparator_10_eq, comparator_11_eq, comparator_12_eq, comparator_13_eq, comparator_14_eq, Dec3f,
       DecMba13, DecMdc15, Inc31, IncMba12, IncMdc14, IsAdd, IsAnd, IsConcatSL1, IsConcatSR1, IsOr, IsSL1,
       IsSR1, IsSub, IsXor, MemDecr, MemIncr, not_1_out, or_9_out, OrBa20, OrImm44, OrMba23, RegOp,
       SubcMba10, SubImm41, SubMba11, XorBa19, XorImm43, XorMba22;

  Comparator comparator_1 (.a(AluOp), .b({8{1'b0}}), .eq(comparator_1_eq));  // open: gt, lt
  Comparator comparator_2 (.a(AluOp), .b(8'h1), .eq(comparator_2_eq));  // open: gt, lt
  Comparator comparator_3 (.a(AluOp), .b(8'h2), .eq(IsConcatSR1));  // open: gt, lt
  Comparator comparator_4 (.a(AluOp), .b(8'h3), .eq(IsConcatSL1));  // open: gt, lt
  Comparator #(.mode("unsigned")) comparator_5 (.a(AluOp), .b(8'h20), .lt(comparator_5_lt));  // open: gt, eq
  or or_1 (MemIncr, IncMba12, IncMdc14);
  or or_2 (MemDecr, DecMba13, DecMdc15);
  or or_3 (IsAnd, AndBa18, AndMba21, AndImm42);
  or or_4 (IsXor, XorBa19, XorMba22, XorImm43);
  // Probe on AluOp[3:1]
  buf or_5 (IsSR1, comparator_1_eq);  // OR_Gate
  buf or_6 (IsSL1, comparator_2_eq);  // OR_Gate
  Comparator #(.mode("unsigned")) comparator_6 (.a(AluOp), .b(8'hf), .gt(comparator_6_gt));  // open: eq, lt
  Comparator #(.mode("unsigned"), .width(3)) comparator_7 (
    .a(AluOp[3:1]), .b(3'b101), .lt(comparator_7_lt));  // open: gt, eq
  // Probe on 3'b101
  and and_1 (RegOp, comparator_6_gt, comparator_5_lt, comparator_7_lt);
  // Probe on AluOp[3:1]
  and and_2 (and_2_out, RegOp, AluOp[0]);
  Comparator #(.width(5)) comparator_8 (.a(AluOp[7:3]), .b(5'b10100), .eq(comparator_8_eq));  // open: gt, lt
  Comparator #(.width(5)) comparator_9 (.a(AluOp[7:3]), .b(5'b10101), .eq(comparator_9_eq));  // open: gt, lt
  Comparator #(.width(5)) comparator_10 (.a(AluOp[7:3]), .b(5'b10110), .eq(comparator_10_eq));  // open: gt, lt
  Comparator #(.width(5)) comparator_11 (.a(AluOp[7:3]), .b(5'b10111), .eq(comparator_11_eq));  // open: gt, lt
  Comparator #(.width(5)) comparator_12 (.a(AluOp[7:3]), .b(5'b11000), .eq(comparator_12_eq));  // open: gt, lt
  Comparator #(.width(5)) comparator_13 (.a(AluOp[7:3]), .b(5'b11001), .eq(comparator_13_eq));  // open: gt, lt
  Comparator #(.width(5)) comparator_14 (.a(AluOp[7:3]), .b(5'b11011), .eq(comparator_14_eq));  // open: gt, lt
  // Probe on ALUControl
  Priority_Encoder #(.select(4)) priority_encoder_1 (
    .in0(IsAdd), .in1(IsSub), .in2(IsAnd), .in3(IsOr), .in4(IsSR1), .in5(IsSL1), .in6(IsConcatSR1),
    .in7(IsConcatSL1), .in8(AddcMba8), .in9(AddMba), .in10(SubcMba10), .in11(SubMba11), .in12(MemIncr),
    .in13(MemDecr), .in14(IsXor), .in15(BCD36), .out(ALUControl));  // open: gs, en_out, en_in
  or or_7 (IsAdd, and_2_out, Inc31, AddImm40, AddImm40);
  and and_3 (and_3_out, RegOp, not_1_out);
  not not_1 (not_1_out, AluOp[0]);
  or or_8 (IsOr, OrBa20, OrMba23, OrImm44);
  or or_9 (or_9_out, comparator_8_eq, comparator_9_eq, comparator_10_eq, comparator_11_eq, comparator_12_eq, comparator_13_eq, comparator_14_eq);
  or or_10 (IsSub, and_3_out, Dec3f, SubImm41, or_9_out);
  // Probe on AluOp[7:3]
  and and_4 (BCD36, ~AluOp[0], AluOp[1], AluOp[2], ~AluOp[3], AluOp[4], AluOp[5], ~AluOp[6], ~AluOp[7]);  // AND_Gate
  and and_5 (AndBa18, ~AluOp[0], AluOp[1], ~AluOp[2], AluOp[3], AluOp[4], ~AluOp[5], ~AluOp[6], ~AluOp[7]);  // AND_Gate
  and and_6 (IncMba12, ~AluOp[0], ~AluOp[1], AluOp[2], AluOp[3], ~AluOp[4], ~AluOp[5], ~AluOp[6], ~AluOp[7]);  // AND_Gate
  and and_7 (IncMdc14, ~AluOp[0], AluOp[1], AluOp[2], AluOp[3], ~AluOp[4], ~AluOp[5], ~AluOp[6], ~AluOp[7]);  // AND_Gate
  and and_8 (AndMba21, AluOp[0], ~AluOp[1], AluOp[2], AluOp[3], AluOp[4], ~AluOp[5], ~AluOp[6], ~AluOp[7]);  // AND_Gate
  and and_9 (OrMba23, AluOp[0], AluOp[1], AluOp[2], AluOp[3], AluOp[4], ~AluOp[5], ~AluOp[6], ~AluOp[7]);  // AND_Gate
  and and_10 (Inc31, AluOp[0], ~AluOp[1], ~AluOp[2], ~AluOp[3], AluOp[4], AluOp[5], ~AluOp[6], ~AluOp[7]);  // AND_Gate
  and and_11 (AddImm40, ~AluOp[0], ~AluOp[1], ~AluOp[2], ~AluOp[3], ~AluOp[4], ~AluOp[5], AluOp[6], ~AluOp[7]);  // AND_Gate
  and and_12 (AndImm42, ~AluOp[0], AluOp[1], ~AluOp[2], ~AluOp[3], ~AluOp[4], ~AluOp[5], AluOp[6], ~AluOp[7]);  // AND_Gate
  and and_13 (OrImm44, ~AluOp[0], ~AluOp[1], AluOp[2], ~AluOp[3], ~AluOp[4], ~AluOp[5], AluOp[6], ~AluOp[7]);  // AND_Gate
  and and_14 (AddcMba8, ~AluOp[0], ~AluOp[1], ~AluOp[2], AluOp[3], ~AluOp[4], ~AluOp[5], ~AluOp[6], ~AluOp[7]);  // AND_Gate
  and and_15 (SubMba11, AluOp[0], AluOp[1], ~AluOp[2], AluOp[3], ~AluOp[4], ~AluOp[5], ~AluOp[6], ~AluOp[7]);  // AND_Gate
  and and_16 (DecMba13, AluOp[0], ~AluOp[1], AluOp[2], AluOp[3], ~AluOp[4], ~AluOp[5], ~AluOp[6], ~AluOp[7]);  // AND_Gate
  and and_17 (DecMdc15, AluOp[0], AluOp[1], AluOp[2], AluOp[3], ~AluOp[4], ~AluOp[5], ~AluOp[6], ~AluOp[7]);  // AND_Gate
  and and_18 (XorMba22, ~AluOp[0], AluOp[1], AluOp[2], AluOp[3], AluOp[4], ~AluOp[5], ~AluOp[6], ~AluOp[7]);  // AND_Gate
  and and_19 (Dec3f, AluOp[0], AluOp[1], AluOp[2], AluOp[3], AluOp[4], AluOp[5], ~AluOp[6], ~AluOp[7]);  // AND_Gate
  and and_20 (SubImm41, AluOp[0], ~AluOp[1], ~AluOp[2], ~AluOp[3], ~AluOp[4], ~AluOp[5], AluOp[6], ~AluOp[7]);  // AND_Gate
  and and_21 (XorImm43, AluOp[0], AluOp[1], ~AluOp[2], ~AluOp[3], ~AluOp[4], ~AluOp[5], AluOp[6], ~AluOp[7]);  // AND_Gate
  and and_22 (SubcMba10, ~AluOp[0], AluOp[1], ~AluOp[2], AluOp[3], ~AluOp[4], ~AluOp[5], ~AluOp[6], ~AluOp[7]);  // AND_Gate
  and and_23 (AddMba, AluOp[0], ~AluOp[1], ~AluOp[2], AluOp[3], ~AluOp[4], ~AluOp[5], ~AluOp[6], ~AluOp[7]);  // AND_Gate
  and and_24 (XorBa19, AluOp[0], AluOp[1], ~AluOp[2], AluOp[3], AluOp[4], ~AluOp[5], ~AluOp[6], ~AluOp[7]);  // AND_Gate
  and and_25 (OrBa20, ~AluOp[0], ~AluOp[1], AluOp[2], AluOp[3], AluOp[4], ~AluOp[5], ~AluOp[6], ~AluOp[7]);  // AND_Gate

  // Other names for the same wires on the sheet: IncDec = AluOp[0]; RegBit[2:0] = AluOp[3:1];
  //   FiveFirstIn16Bits[4:0] = AluOp[7:3]; Double_Add = AddcMba8; IsBCD = BCD36; MemAdd = AddMba;
  //   SubMemCF = SubcMba10; SubMem = SubMba11
endmodule
